// Digital circuit barrelShifter.dig as structural Verilog
// Barrel-Shifter with selectable bit width.
// {{de Barrel-Shifter mit wählbarer Bitbreite.}}
module barrelShifter (
  input  [15:0] D_in,
  input  [3:0] sh,
  output [15:0] D
);

  shift_inc #(.generic("dataBits:=16; shiftBits:=int(4); dir:=\"left\"; if (isPresent(args)) { dir=args.dir; dataBits=args.dataBits; shiftBits=bitsNeededFor(args.dataBits-1); }")) shift_inc_1 (
    .D_in(D_in), .sh(sh), .D(D));
endmodule
