// Digital circuit Interrupt.dig as structural Verilog
// Simple interrupt controller.
// If an interrupt is triggered, the controller is disabled: no 
// further interrupts can be triggered. Setting the input reti 
// releases the interrupt controller.
// {{de Einfacher Interrupt-Controller.
// Wird ein Interrupt ausgelöst, wird der Controller
// gesperrt: Es können keine weiteren Interrupts
// ausgelöst werden. Erst der Eingang reti gibt den 
// Interrupt-Controller wieder frei.}}
module Interrupt (
  input  nie,
  input  C,
  input  imm,
  input  reti,
  input  intr,
  output iEn
);

  wire intLock_nq, intReq_q;

  JK_FF intLock (.J(iEn), .C(~C), .K(reti), .nQ(intLock_nq));  // open: Q
  JK_FF intReq (.J(intr), .C(~C), .K(reti), .Q(intReq_q));  // open: nQ
  and and_1 (iEn, intLock_nq, ~imm, intReq_q, ~nie);  // And

  // Notes on the sheet:
  //   iEn: interrupt trigger used by the PC
  //   {{de Interrupt-Freigabe für PC}}
  //   imm: immediate register:
  //   If set, an interrupt is blocked.
  //   {{de Immediate Register:
  //   Wenn gesetzt, wird Interrupt verhindert.}}
  //   reti: return from interrupt. This signal is used to 
  //   release the interrupt controller.
  //   {{de return from interrupt. Über dieses Signal werden
  //   die Interrupts wieder freigegeben.}}
  //   intr: interrupt trigger {{de Interrupt Anforderung}}
endmodule
